// Logisim project 11.circ as structural Verilog: 1 circuit, main circuit main
module main (
  input  ADDRESS1,
  input  ADDRESS2,
  input  ADDRESS3,
  input  Data_in1,
  input  Data_in2,
  input  Data_in3,
  input  Data_in4,
  input  Mode_input_pin,
  output Data_out1,
  output Data_out2,
  output Data_out3,
  output Data_out4
);

  wire and_1_out, and_2_out, and_3_out, and_4_out, and_5_out, and_6_out, and_7_out, and_8_out, and_9_out,
       and_10_out, and_11_out, and_12_out, and_13_out, and_14_out, and_15_out, and_16_out, and_17_out,
       and_18_out, and_19_out, and_20_out, and_21_out, and_22_out, and_23_out, and_24_out, and_25_out,
       and_26_out, and_27_out, and_28_out, and_29_out, and_30_out, and_31_out, and_32_out, and_33_out,
       and_34_out, and_35_out, and_36_out, and_37_out, and_38_out, and_39_out, and_40_out, and_41_out,
       and_42_out, and_43_out, and_44_out, and_45_out, and_46_out, and_47_out, and_48_out, and_49_out,
       and_50_out, and_51_out, and_52_out, and_53_out, and_54_out, and_55_out, and_56_out, and_57_out,
       and_58_out, and_59_out, and_60_out, and_61_out, and_62_out, and_63_out, and_64_out, and_65_out,
       and_66_out, and_67_out, and_68_out, and_69_out, and_70_out, and_71_out, and_72_out, and_73_out,
       and_74_out, and_75_out, and_76_out, and_77_out, and_78_out, and_79_out, and_80_out, and_81_out,
       and_82_out, and_83_out, and_84_out, and_85_out, and_86_out, and_87_out, and_88_out, clock_1_out,
       clock_2_out, clock_3_out, clock_4_out, clock_5_out, clock_6_out, clock_7_out, clock_8_out, d_ff_1_q,
       d_ff_2_q, d_ff_3_q, d_ff_4_q, d_ff_5_q, d_ff_6_q, d_ff_7_q, d_ff_8_q, d_ff_9_q, d_ff_10_q, d_ff_11_q,
       d_ff_12_q, d_ff_13_q, d_ff_14_q, d_ff_15_q, d_ff_16_q, d_ff_17_q, d_ff_18_q, d_ff_19_q, d_ff_20_q,
       d_ff_21_q, d_ff_22_q, d_ff_23_q, d_ff_24_q, d_ff_25_q, d_ff_26_q, d_ff_27_q, d_ff_28_q, d_ff_29_q,
       d_ff_30_q, d_ff_31_q, d_ff_32_q, d_ff_33_q, d_ff_34_q, d_ff_35_q, d_ff_36_q, d_ff_37_q, d_ff_38_q,
       d_ff_39_q, d_ff_40_q, d_ff_41_q, d_ff_42_q, d_ff_43_q, d_ff_44_q, d_ff_45_q, d_ff_46_q, d_ff_47_q,
       d_ff_48_q, d_ff_49_q, d_ff_50_q, d_ff_51_q, d_ff_52_q, d_ff_53_q, d_ff_54_q, d_ff_55_q, d_ff_56_q,
       d_ff_57_q, d_ff_58_q, d_ff_59_q, d_ff_60_q, d_ff_61_q, d_ff_62_q, d_ff_63_q, d_ff_64_q, not_1_out,
       not_2_out, not_3_out, not_4_out, not_5_out, not_6_out, not_7_out, not_8_out, not_9_out, not_10_out,
       not_11_out, not_12_out, not_13_out, not_14_out, not_15_out, not_16_out, not_17_out, not_18_out,
       not_19_out, not_20_out, undriven;

  not not_1 (not_1_out, ADDRESS1);
  not not_2 (not_2_out, ADDRESS2);
  not not_3 (not_3_out, ADDRESS3);
  not not_4 (not_4_out, ADDRESS3);
  not not_5 (not_5_out, ADDRESS2);
  not not_6 (not_6_out, ADDRESS2);
  not not_7 (not_7_out, ADDRESS1);
  Clock clock_1 (.out(clock_1_out));
  not not_8 (not_8_out, ADDRESS3);
  not not_9 (not_9_out, ADDRESS1);
  not not_10 (not_10_out, ADDRESS3);
  not not_11 (not_11_out, ADDRESS2);
  not not_12 (not_12_out, ADDRESS1);
  Clock clock_2 (.out(clock_2_out));
  and and_1 (and_1_out, ADDRESS3, ADDRESS2, ADDRESS1);
  Clock clock_3 (.out(clock_3_out));
  and and_2 (and_2_out, ADDRESS3, ADDRESS2, not_1_out);
  Clock clock_4 (.out(clock_4_out));
  and and_3 (and_3_out, ADDRESS3, not_2_out, ADDRESS1);
  Clock clock_5 (.out(clock_5_out));
  and and_4 (and_4_out, not_3_out, ADDRESS2, ADDRESS1);
  Clock clock_6 (.out(clock_6_out));
  and and_5 (and_5_out, not_4_out, not_5_out, ADDRESS1);
  Clock clock_7 (.out(clock_7_out));
  and and_6 (and_6_out, ADDRESS3, not_6_out, not_7_out);
  and and_7 (and_7_out, not_8_out, ADDRESS2, not_9_out);
  Clock clock_8 (.out(clock_8_out));
  and and_8 (and_8_out, not_10_out, not_11_out, not_12_out);
  and and_9 (and_9_out, clock_2_out, and_1_out);
  and and_10 (and_10_out, clock_3_out, and_2_out);
  and and_11 (and_11_out, clock_4_out, and_3_out);
  and and_12 (and_12_out, clock_5_out, and_4_out);
  and and_13 (and_13_out, clock_6_out, and_5_out);
  and and_14 (and_14_out, clock_7_out, and_6_out);
  and and_15 (and_15_out, clock_1_out, and_7_out);
  and and_16 (and_16_out, Mode_input_pin, and_12_out);
  and and_17 (and_17_out, clock_8_out, and_8_out);
  and and_18 (and_18_out, Mode_input_pin, and_9_out);
  and and_19 (and_19_out, Mode_input_pin, and_10_out);
  and and_20 (and_20_out, Mode_input_pin, and_11_out);
  and and_21 (and_21_out, Mode_input_pin, and_13_out);
  and and_22 (and_22_out, Mode_input_pin, and_14_out);
  and and_23 (and_23_out, Mode_input_pin, and_15_out);
  and and_24 (and_24_out, Mode_input_pin, and_17_out);
  D_Flip_Flop d_ff_1 (.D(Data_in1), .clk(and_20_out), .Q(d_ff_1_q));  // open: Qn, preset, reset
  D_Flip_Flop d_ff_2 (.D(Data_in2), .clk(and_20_out), .Q(d_ff_2_q));  // open: Qn, preset, reset
  D_Flip_Flop d_ff_3 (.D(Data_in3), .clk(and_20_out), .Q(d_ff_3_q));  // open: Qn, preset, reset
  D_Flip_Flop d_ff_4 (.D(Data_in4), .clk(and_20_out), .Q(d_ff_4_q));  // open: Qn, preset, reset
  D_Flip_Flop d_ff_5 (.D(Data_in1), .clk(and_16_out), .Q(d_ff_5_q));  // open: Qn, preset, reset
  D_Flip_Flop d_ff_6 (.D(Data_in2), .clk(and_16_out), .Q(d_ff_6_q));  // open: Qn, preset, reset
  D_Flip_Flop d_ff_7 (.D(Data_in3), .clk(and_16_out), .Q(d_ff_7_q));  // open: Qn, preset, reset
  D_Flip_Flop d_ff_8 (.D(Data_in4), .clk(and_16_out), .Q(d_ff_8_q));  // open: Qn, preset, reset
  D_Flip_Flop d_ff_9 (.D(Data_in1), .clk(and_21_out), .Q(d_ff_9_q));  // open: Qn, preset, reset
  D_Flip_Flop d_ff_10 (.D(Data_in2), .clk(and_21_out), .Q(d_ff_10_q));  // open: Qn, preset, reset
  D_Flip_Flop d_ff_11 (.D(Data_in3), .clk(and_21_out), .Q(d_ff_11_q));  // open: Qn, preset, reset
  D_Flip_Flop d_ff_12 (.D(Data_in4), .clk(and_21_out), .Q(d_ff_12_q));  // open: Qn, preset, reset
  D_Flip_Flop d_ff_13 (.D(Data_in1), .clk(and_18_out), .Q(d_ff_13_q));  // open: Qn, preset, reset
  D_Flip_Flop d_ff_14 (.D(Data_in2), .clk(and_18_out), .Q(d_ff_14_q));  // open: Qn, preset, reset
  D_Flip_Flop d_ff_15 (.D(Data_in1), .clk(and_19_out), .Q(d_ff_15_q));  // open: Qn, preset, reset
  D_Flip_Flop d_ff_16 (.D(Data_in2), .clk(and_19_out), .Q(d_ff_16_q));  // open: Qn, preset, reset
  D_Flip_Flop d_ff_17 (.D(Data_in3), .clk(and_19_out), .Q(d_ff_17_q));  // open: Qn, preset, reset
  D_Flip_Flop d_ff_18 (.D(Data_in4), .clk(and_19_out), .Q(d_ff_18_q));  // open: Qn, preset, reset
  D_Flip_Flop d_ff_19 (.D(Data_in1), .clk(and_22_out), .Q(d_ff_19_q));  // open: Qn, preset, reset
  D_Flip_Flop d_ff_20 (.D(Data_in2), .clk(and_22_out), .Q(d_ff_20_q));  // open: Qn, preset, reset
  D_Flip_Flop d_ff_21 (.D(Data_in3), .clk(and_22_out), .Q(d_ff_21_q));  // open: Qn, preset, reset
  D_Flip_Flop d_ff_22 (.D(Data_in4), .clk(and_22_out), .Q(d_ff_22_q));  // open: Qn, preset, reset
  D_Flip_Flop d_ff_23 (.D(Data_in1), .clk(and_23_out), .Q(d_ff_23_q));  // open: Qn, preset, reset
  D_Flip_Flop d_ff_24 (.D(Data_in2), .clk(and_23_out), .Q(d_ff_24_q));  // open: Qn, preset, reset
  D_Flip_Flop d_ff_25 (.D(Data_in3), .clk(and_23_out), .Q(d_ff_25_q));  // open: Qn, preset, reset
  D_Flip_Flop d_ff_26 (.D(Data_in4), .clk(and_23_out), .Q(d_ff_26_q));  // open: Qn, preset, reset
  D_Flip_Flop d_ff_27 (.D(Data_in1), .clk(and_24_out), .Q(d_ff_27_q));  // open: Qn, preset, reset
  D_Flip_Flop d_ff_28 (.D(Data_in2), .clk(and_24_out), .Q(d_ff_28_q));  // open: Qn, preset, reset
  D_Flip_Flop d_ff_29 (.D(Data_in3), .clk(and_24_out), .Q(d_ff_29_q));  // open: Qn, preset, reset
  D_Flip_Flop d_ff_30 (.D(Data_in4), .clk(and_24_out), .Q(d_ff_30_q));  // open: Qn, preset, reset
  D_Flip_Flop d_ff_31 (.D(Data_in3), .clk(and_18_out), .Q(d_ff_31_q));  // open: Qn, preset, reset
  D_Flip_Flop d_ff_32 (.D(Data_in4), .clk(and_18_out), .Q(d_ff_32_q));  // open: Qn, preset, reset
  not not_13 (not_13_out, Mode_input_pin);
  not not_14 (not_14_out, Mode_input_pin);
  not not_15 (not_15_out, Mode_input_pin);
  not not_16 (not_16_out, Mode_input_pin);
  not not_17 (not_17_out, Mode_input_pin);
  not not_18 (not_18_out, Mode_input_pin);
  not not_19 (not_19_out, Mode_input_pin);
  not not_20 (not_20_out, Mode_input_pin);
  and and_25 (and_25_out, d_ff_18_q, not_17_out);
  and and_26 (and_26_out, d_ff_1_q, not_13_out);
  and and_27 (and_27_out, d_ff_2_q, not_13_out);
  and and_28 (and_28_out, d_ff_3_q, not_13_out);
  and and_29 (and_29_out, d_ff_4_q, not_13_out);
  and and_30 (and_30_out, d_ff_5_q, not_14_out);
  and and_31 (and_31_out, d_ff_6_q, not_14_out);
  and and_32 (and_32_out, d_ff_7_q, not_14_out);
  and and_33 (and_33_out, d_ff_8_q, not_14_out);
  and and_34 (and_34_out, d_ff_9_q, not_15_out);
  and and_35 (and_35_out, d_ff_10_q, not_15_out);
  and and_36 (and_36_out, d_ff_11_q, not_15_out);
  and and_37 (and_37_out, d_ff_12_q, not_15_out);
  and and_38 (and_38_out, d_ff_19_q, not_18_out);
  and and_39 (and_39_out, d_ff_20_q, not_18_out);
  and and_40 (and_40_out, d_ff_21_q, not_18_out);
  and and_41 (and_41_out, d_ff_22_q, not_18_out);
  and and_42 (and_42_out, d_ff_23_q, not_19_out);
  and and_43 (and_43_out, d_ff_24_q, not_19_out);
  and and_44 (and_44_out, d_ff_25_q, not_19_out);
  and and_45 (and_45_out, d_ff_26_q, not_19_out);
  and and_46 (and_46_out, d_ff_27_q, not_20_out);
  and and_47 (and_47_out, d_ff_28_q, not_20_out);
  and and_48 (and_48_out, d_ff_29_q, not_20_out);
  and and_49 (and_49_out, d_ff_30_q, not_20_out);
  and and_50 (and_50_out, d_ff_13_q, not_16_out);
  and and_51 (and_51_out, d_ff_14_q, not_16_out);
  and and_52 (and_52_out, d_ff_31_q, not_16_out);
  and and_53 (and_53_out, d_ff_32_q, not_16_out);
  and and_54 (and_54_out, d_ff_15_q, not_17_out);
  and and_55 (and_55_out, d_ff_16_q, not_17_out);
  and and_56 (and_56_out, d_ff_17_q, not_17_out);
  D_Flip_Flop d_ff_33 (.D(and_26_out), .clk(and_11_out), .Q(d_ff_33_q));  // open: Qn, preset, reset
  D_Flip_Flop d_ff_34 (.D(and_27_out), .clk(and_11_out), .Q(d_ff_34_q));  // open: Qn, preset, reset
  D_Flip_Flop d_ff_35 (.D(and_28_out), .clk(and_11_out), .Q(d_ff_35_q));  // open: Qn, preset, reset
  D_Flip_Flop d_ff_36 (.D(and_29_out), .clk(and_11_out), .Q(d_ff_36_q));  // open: Qn, preset, reset
  D_Flip_Flop d_ff_37 (.D(and_30_out), .clk(and_12_out), .Q(d_ff_37_q));  // open: Qn, preset, reset
  D_Flip_Flop d_ff_38 (.D(and_31_out), .clk(and_12_out), .Q(d_ff_38_q));  // open: Qn, preset, reset
  D_Flip_Flop d_ff_39 (.D(and_32_out), .clk(and_12_out), .Q(d_ff_39_q));  // open: Qn, preset, reset
  D_Flip_Flop d_ff_40 (.D(and_33_out), .clk(and_12_out), .Q(d_ff_40_q));  // open: Qn, preset, reset
  D_Flip_Flop d_ff_41 (.D(and_34_out), .clk(and_13_out), .Q(d_ff_41_q));  // open: Qn, preset, reset
  D_Flip_Flop d_ff_42 (.D(and_35_out), .clk(and_13_out), .Q(d_ff_42_q));  // open: Qn, preset, reset
  D_Flip_Flop d_ff_43 (.D(and_36_out), .clk(and_13_out), .Q(d_ff_43_q));  // open: Qn, preset, reset
  D_Flip_Flop d_ff_44 (.D(and_37_out), .clk(and_13_out), .Q(d_ff_44_q));  // open: Qn, preset, reset
  D_Flip_Flop d_ff_45 (.D(and_38_out), .clk(and_14_out), .Q(d_ff_45_q));  // open: Qn, preset, reset
  D_Flip_Flop d_ff_46 (.D(and_39_out), .clk(and_14_out), .Q(d_ff_46_q));  // open: Qn, preset, reset
  D_Flip_Flop d_ff_47 (.D(and_40_out), .clk(and_14_out), .Q(d_ff_47_q));  // open: Qn, preset, reset
  D_Flip_Flop d_ff_48 (.D(and_41_out), .clk(and_14_out), .Q(d_ff_48_q));  // open: Qn, preset, reset
  D_Flip_Flop d_ff_49 (.D(and_42_out), .clk(and_15_out), .Q(d_ff_49_q));  // open: Qn, preset, reset
  D_Flip_Flop d_ff_50 (.D(and_43_out), .clk(and_15_out), .Q(d_ff_50_q));  // open: Qn, preset, reset
  D_Flip_Flop d_ff_51 (.D(and_44_out), .clk(and_15_out), .Q(d_ff_51_q));  // open: Qn, preset, reset
  D_Flip_Flop d_ff_52 (.D(and_45_out), .clk(and_15_out), .Q(d_ff_52_q));  // open: Qn, preset, reset
  D_Flip_Flop d_ff_53 (.D(and_46_out), .clk(and_17_out), .Q(d_ff_53_q));  // open: Qn, preset, reset
  D_Flip_Flop d_ff_54 (.D(and_47_out), .clk(and_17_out), .Q(d_ff_54_q));  // open: Qn, preset, reset
  D_Flip_Flop d_ff_55 (.D(and_48_out), .clk(and_17_out), .Q(d_ff_55_q));  // open: Qn, preset, reset
  D_Flip_Flop d_ff_56 (.D(and_49_out), .clk(and_17_out), .Q(d_ff_56_q));  // open: Qn, preset, reset
  D_Flip_Flop d_ff_57 (.D(and_50_out), .clk(and_9_out), .Q(d_ff_57_q), .preset(undriven));  // open: Qn, reset
  D_Flip_Flop d_ff_58 (.D(and_51_out), .clk(and_9_out), .Q(d_ff_58_q));  // open: Qn, preset, reset
  D_Flip_Flop d_ff_59 (.D(and_52_out), .clk(and_9_out), .Q(d_ff_59_q));  // open: Qn, preset, reset
  D_Flip_Flop d_ff_60 (.D(and_53_out), .clk(and_9_out), .Q(d_ff_60_q));  // open: Qn, preset, reset
  D_Flip_Flop d_ff_61 (.D(and_54_out), .clk(and_10_out), .Q(d_ff_61_q));  // open: Qn, preset, reset
  D_Flip_Flop d_ff_62 (.D(and_55_out), .clk(and_10_out), .Q(d_ff_62_q));  // open: Qn, preset, reset
  D_Flip_Flop d_ff_63 (.D(and_56_out), .clk(and_10_out), .Q(d_ff_63_q));  // open: Qn, preset, reset
  D_Flip_Flop d_ff_64 (.D(and_25_out), .clk(and_10_out), .Q(d_ff_64_q));  // open: Qn, preset, reset
  and and_57 (and_57_out, d_ff_61_q, and_2_out);
  and and_58 (and_58_out, d_ff_62_q, and_2_out);
  and and_59 (and_59_out, d_ff_63_q, and_2_out);
  and and_60 (and_60_out, d_ff_64_q, and_2_out);
  and and_61 (and_61_out, d_ff_33_q, and_3_out);
  and and_62 (and_62_out, d_ff_34_q, and_3_out);
  and and_63 (and_63_out, d_ff_35_q, and_3_out);
  and and_64 (and_64_out, d_ff_36_q, and_3_out);
  and and_65 (and_65_out, d_ff_37_q, and_4_out);
  and and_66 (and_66_out, d_ff_38_q, and_4_out);
  and and_67 (and_67_out, d_ff_39_q, and_4_out);
  and and_68 (and_68_out, d_ff_40_q, and_4_out);
  and and_69 (and_69_out, d_ff_41_q, and_5_out);
  and and_70 (and_70_out, d_ff_42_q, and_5_out);
  and and_71 (and_71_out, d_ff_43_q, and_5_out);
  and and_72 (and_72_out, d_ff_44_q, and_5_out);
  and and_73 (and_73_out, d_ff_45_q, and_6_out);
  and and_74 (and_74_out, d_ff_46_q, and_6_out);
  and and_75 (and_75_out, d_ff_47_q, and_6_out);
  and and_76 (and_76_out, d_ff_48_q, and_6_out);
  and and_77 (and_77_out, d_ff_49_q, and_7_out);
  and and_78 (and_78_out, d_ff_50_q, and_7_out);
  and and_79 (and_79_out, d_ff_51_q, and_7_out);
  and and_80 (and_80_out, d_ff_52_q, and_7_out);
  and and_81 (and_81_out, d_ff_53_q, and_8_out);
  and and_82 (and_82_out, d_ff_54_q, and_8_out);
  and and_83 (and_83_out, d_ff_55_q, and_8_out);
  and and_84 (and_84_out, d_ff_56_q, and_8_out);
  and and_85 (and_85_out, d_ff_57_q, and_1_out);
  and and_86 (and_86_out, d_ff_58_q, and_1_out);
  and and_87 (and_87_out, d_ff_59_q, and_1_out);
  and and_88 (and_88_out, d_ff_60_q, and_1_out);
  or or_1 (Data_out1, and_85_out, and_57_out, and_61_out, and_65_out, and_69_out, and_73_out, and_77_out, and_81_out);
  or or_2 (Data_out2, and_86_out, and_58_out, and_62_out, and_66_out, and_70_out, and_74_out, and_78_out, and_82_out);
  or or_3 (Data_out3, and_87_out, and_59_out, and_63_out, and_67_out, and_71_out, and_75_out, and_79_out, and_83_out);
  or or_4 (Data_out4, and_88_out, and_60_out, and_64_out, and_68_out, and_72_out, and_76_out, and_80_out, and_84_out);

  // Other names for the same wires on the sheet: Di1 = Data_in1; Di2 = Data_in2; Di3 = Data_in3; Di4 = Data_in4;
  //   Do1 = Data_out1; Do2 = Data_out2; Do3 = Data_out3; Do4 = Data_out4; M = Mode_input_pin

  // Notes on the sheet:
  //   Doris Lu Wang
  //   ID:260952214
endmodule
