// Logisim project a4.circ as structural Verilog: 1 circuit, main circuit main
module main (
  input  A,
  input  B,
  input  C,
  input  X,
  input  Y,
  input  Z,
  output W,
  output V
);

  wire and_1_out, and_2_out, clock_1_out, clock_2_out, not_1_out;

  // NoConnect on B
  not not_1 (not_1_out, Y);
  Clock clock_1 (.out(clock_1_out));
  Clock clock_2 (.out(clock_2_out));
  and and_1 (and_1_out, X, not_1_out, clock_2_out, Z);
  and and_2 (and_2_out, X, clock_2_out, Y, Z);
  and and_3 (W, A, clock_1_out, C);
  or or_1 (V, and_1_out, and_2_out);

  // Notes on the sheet:
  //   Ziming Dong
  //   Student ID: 260951177
endmodule
