// Logisim project a5.circ as structural Verilog: 1 circuit, main circuit main
module main (
  input  R_W,
  input  Address1,
  input  Address2,
  input  Address3,
  input  DataIn1,
  input  DataIn2,
  input  DataIn3,
  input  DataIn4,
  output DataOut1,
  output DataOut2,
  output DataOut3,
  output DataOut4
);

  wire and_17_out, and_18_out, and_19_out, and_20_out, and_21_out, and_22_out, and_23_out, and_24_out,
       and_25_out, and_26_out, and_27_out, and_28_out, and_29_out, and_30_out, and_31_out, and_32_out,
       and_33_out, and_34_out, and_35_out, and_36_out, and_37_out, and_38_out, and_39_out, and_40_out,
       and_41_out, and_42_out, and_43_out, and_44_out, and_45_out, and_46_out, and_47_out, and_48_out,
       and_49_out, and_50_out, and_51_out, and_52_out, and_53_out, and_54_out, and_55_out, and_56_out, CLK,
       d01, d02, d03, d04, d11, d12, d13, d14, d21, d22, d23, d24, d31, d32, d33, d34, d41, d42, d43, d44,
       d51, d52, d53, d54, d61, d62, d63, d64, d71, d72, d73, d74, d_ff_1_q, d_ff_2_q, d_ff_3_q, d_ff_4_q,
       d_ff_5_q, d_ff_6_q, d_ff_7_q, d_ff_8_q, d_ff_9_q, d_ff_10_q, d_ff_11_q, d_ff_12_q, d_ff_13_q,
       d_ff_14_q, d_ff_15_q, d_ff_16_q, d_ff_17_q, d_ff_18_q, d_ff_19_q, d_ff_20_q, d_ff_21_q, d_ff_22_q,
       d_ff_23_q, d_ff_24_q, d_ff_25_q, d_ff_26_q, d_ff_27_q, d_ff_28_q, d_ff_29_q, d_ff_30_q, d_ff_31_q,
       d_ff_32_q, d_ff_33_q, d_ff_34_q, d_ff_35_q, d_ff_36_q, d_ff_37_q, d_ff_38_q, d_ff_39_q, d_ff_40_q,
       d_ff_41_q, d_ff_42_q, d_ff_43_q, d_ff_44_q, d_ff_45_q, d_ff_46_q, d_ff_47_q, d_ff_48_q, d_ff_49_q,
       d_ff_50_q, d_ff_51_q, d_ff_52_q, d_ff_53_q, d_ff_54_q, d_ff_55_q, d_ff_56_q, d_ff_57_q, d_ff_58_q,
       d_ff_59_q, d_ff_60_q, d_ff_61_q, d_ff_62_q, d_ff_63_q, d_ff_64_q, not_1_out, not_2_out, not_3_out,
       not_4_out, not_5_out, not_6_out, not_7_out, not_8_out, not_9_out, not_10_out, not_11_out, not_12_out,
       not_13_out, not_14_out, not_15_out, not_16_out, not_17_out, not_18_out, not_19_out, not_20_out, R0,
       r0_t, R1, r1_t, R2, r2_t, R3, r3_t, R4, r4_t, R5, r5_t, R6, r6_t, R7, r7_t, undriven, undriven_2;

  not not_1 (not_1_out, Address1);
  not not_2 (not_2_out, Address2);
  not not_3 (not_3_out, Address3);
  not not_4 (not_4_out, Address1);
  not not_5 (not_5_out, Address2);
  not not_6 (not_6_out, Address1);
  not not_7 (not_7_out, Address3);
  not not_8 (not_8_out, Address2);
  not not_9 (not_9_out, Address3);
  not not_10 (not_10_out, Address1);
  not not_11 (not_11_out, Address2);
  not not_12 (not_12_out, Address3);
  and and_1 (r0_t, not_1_out, Address2, Address3);
  and and_2 (r1_t, Address1, not_2_out, Address3);
  and and_3 (r2_t, Address1, Address2, not_3_out);
  and and_4 (r3_t, not_4_out, not_5_out, Address3);
  and and_5 (r4_t, not_6_out, Address2, not_7_out);
  and and_6 (r5_t, Address1, not_8_out, not_9_out);
  and and_7 (r6_t, not_10_out, not_11_out, not_12_out);
  and and_8 (r7_t, Address1, Address2, Address3);
  Clock clock_1 (.out(CLK));
  and and_9 (R0, r0_t, CLK);
  and and_10 (R1, r1_t, CLK);
  and and_11 (R2, r2_t, CLK);
  and and_12 (R3, r3_t, CLK);
  and and_13 (R4, r4_t, CLK);
  and and_14 (R5, r5_t, CLK);
  and and_15 (R6, r6_t, CLK);
  and and_16 (R7, r7_t, CLK);
  and and_17 (and_17_out, R0, R_W);
  and and_18 (and_18_out, R1, R_W);
  and and_19 (and_19_out, R2, R_W);
  and and_20 (and_20_out, R3, R_W);
  and and_21 (and_21_out, R4, R_W);
  and and_22 (and_22_out, R5, R_W);
  and and_23 (and_23_out, R6, R_W);
  and and_24 (and_24_out, R7, R_W);
  D_Flip_Flop #(.trigger("falling")) d_ff_1 (.D(DataIn1), .clk(and_17_out), .Q(d_ff_1_q));  // open: Qn, preset, reset
  D_Flip_Flop #(.trigger("falling")) d_ff_2 (.D(DataIn2), .clk(and_17_out), .Q(d_ff_2_q));  // open: Qn, preset, reset
  D_Flip_Flop #(.trigger("falling")) d_ff_3 (.D(DataIn3), .clk(and_17_out), .Q(d_ff_3_q));  // open: Qn, preset, reset
  D_Flip_Flop #(.trigger("falling")) d_ff_4 (.D(DataIn4), .clk(and_17_out), .Q(d_ff_4_q));  // open: Qn, preset, reset
  D_Flip_Flop #(.trigger("falling")) d_ff_5 (.D(DataIn1), .clk(and_18_out), .Q(d_ff_5_q));  // open: Qn, preset, reset
  D_Flip_Flop #(.trigger("falling")) d_ff_6 (.D(DataIn2), .clk(and_18_out), .Q(d_ff_6_q));  // open: Qn, preset, reset
  D_Flip_Flop #(.trigger("falling")) d_ff_7 (.D(DataIn3), .clk(and_18_out), .Q(d_ff_7_q));  // open: Qn, preset, reset
  D_Flip_Flop #(.trigger("falling")) d_ff_8 (.D(DataIn4), .clk(and_18_out), .Q(d_ff_8_q));  // open: Qn, preset, reset
  D_Flip_Flop #(.trigger("falling")) d_ff_9 (.D(DataIn1), .clk(and_19_out), .Q(d_ff_9_q));  // open: Qn, preset, reset
  D_Flip_Flop #(.trigger("falling")) d_ff_10 (.D(DataIn2), .clk(and_19_out), .Q(d_ff_10_q));  // open: Qn, preset, reset
  D_Flip_Flop #(.trigger("falling")) d_ff_11 (.D(DataIn3), .clk(and_19_out), .Q(d_ff_11_q));  // open: Qn, preset, reset
  D_Flip_Flop #(.trigger("falling")) d_ff_12 (.D(DataIn4), .clk(and_19_out), .Q(d_ff_12_q));  // open: Qn, preset, reset
  D_Flip_Flop #(.trigger("falling")) d_ff_13 (.D(DataIn1), .clk(and_20_out), .Q(d_ff_13_q));  // open: Qn, preset, reset
  D_Flip_Flop #(.trigger("falling")) d_ff_14 (.D(DataIn2), .clk(and_20_out), .Q(d_ff_14_q));  // open: Qn, preset, reset
  D_Flip_Flop #(.trigger("falling")) d_ff_15 (.D(DataIn3), .clk(and_20_out), .Q(d_ff_15_q));  // open: Qn, preset, reset
  D_Flip_Flop #(.trigger("falling")) d_ff_16 (.D(DataIn4), .clk(and_20_out), .Q(d_ff_16_q));  // open: Qn, preset, reset
  D_Flip_Flop #(.trigger("falling")) d_ff_17 (.D(DataIn1), .clk(and_21_out), .Q(d_ff_17_q));  // open: Qn, preset, reset
  D_Flip_Flop #(.trigger("falling")) d_ff_18 (.D(DataIn2), .clk(and_21_out), .Q(d_ff_18_q));  // open: Qn, preset, reset
  D_Flip_Flop #(.trigger("falling")) d_ff_19 (.D(DataIn3), .clk(and_21_out), .Q(d_ff_19_q));  // open: Qn, preset, reset
  D_Flip_Flop #(.trigger("falling")) d_ff_20 (.D(DataIn4), .clk(and_21_out), .Q(d_ff_20_q));  // open: Qn, preset, reset
  D_Flip_Flop #(.trigger("falling")) d_ff_21 (.D(DataIn1), .clk(and_22_out), .Q(d_ff_21_q));  // open: Qn, preset, reset
  D_Flip_Flop #(.trigger("falling")) d_ff_22 (.D(DataIn2), .clk(and_22_out), .Q(d_ff_22_q));  // open: Qn, preset, reset
  D_Flip_Flop #(.trigger("falling")) d_ff_23 (.D(DataIn3), .clk(and_22_out), .Q(d_ff_23_q));  // open: Qn, preset, reset
  D_Flip_Flop #(.trigger("falling")) d_ff_24 (.D(DataIn4), .clk(and_22_out), .Q(d_ff_24_q));  // open: Qn, preset, reset
  D_Flip_Flop #(.trigger("falling")) d_ff_25 (.D(DataIn1), .clk(and_23_out), .Q(d_ff_25_q));  // open: Qn, preset, reset
  D_Flip_Flop #(.trigger("falling")) d_ff_26 (.D(DataIn2), .clk(and_23_out), .Q(d_ff_26_q));  // open: Qn, preset, reset
  D_Flip_Flop #(.trigger("falling")) d_ff_27 (.D(DataIn3), .clk(and_23_out), .Q(d_ff_27_q));  // open: Qn, preset, reset
  D_Flip_Flop #(.trigger("falling")) d_ff_28 (.D(DataIn4), .clk(and_23_out), .Q(d_ff_28_q));  // open: Qn, preset, reset
  D_Flip_Flop #(.trigger("falling")) d_ff_29 (.D(DataIn1), .clk(and_24_out), .Q(d_ff_29_q));  // open: Qn, preset, reset
  D_Flip_Flop #(.trigger("falling")) d_ff_30 (.D(DataIn2), .clk(and_24_out), .Q(d_ff_30_q));  // open: Qn, preset, reset
  D_Flip_Flop #(.trigger("falling")) d_ff_31 (.D(DataIn3), .clk(and_24_out), .Q(d_ff_31_q));  // open: Qn, preset, reset
  D_Flip_Flop #(.trigger("falling")) d_ff_32 (.D(DataIn4), .clk(and_24_out), .Q(d_ff_32_q));  // open: Qn, preset, reset
  not not_13 (not_13_out, R_W);
  not not_14 (not_14_out, R_W);
  not not_15 (not_15_out, R_W);
  not not_16 (not_16_out, R_W);
  not not_17 (not_17_out, R_W);
  not not_18 (not_18_out, R_W);
  not not_19 (not_19_out, R_W);
  not not_20 (not_20_out, R_W);
  and and_25 (and_25_out, d_ff_1_q, not_13_out);
  and and_26 (and_26_out, d_ff_2_q, not_13_out);
  and and_27 (and_27_out, d_ff_3_q, not_13_out);
  and and_28 (and_28_out, d_ff_4_q, not_13_out);
  and and_29 (and_29_out, d_ff_5_q, not_14_out);
  and and_30 (and_30_out, d_ff_6_q, not_14_out);
  and and_31 (and_31_out, d_ff_7_q, not_14_out);
  and and_32 (and_32_out, d_ff_8_q, not_14_out);
  and and_33 (and_33_out, d_ff_9_q, not_15_out);
  and and_34 (and_34_out, d_ff_10_q, not_15_out);
  and and_35 (and_35_out, d_ff_11_q, not_15_out);
  and and_36 (and_36_out, d_ff_12_q, not_15_out);
  and and_37 (and_37_out, d_ff_13_q, not_16_out);
  and and_38 (and_38_out, d_ff_14_q, not_16_out);
  and and_39 (and_39_out, d_ff_15_q, not_16_out);
  and and_40 (and_40_out, d_ff_16_q, not_16_out);
  and and_41 (and_41_out, d_ff_17_q, not_17_out);
  and and_42 (and_42_out, d_ff_18_q, not_17_out);
  and and_43 (and_43_out, d_ff_19_q, not_17_out);
  and and_44 (and_44_out, d_ff_20_q, not_17_out);
  and and_45 (and_45_out, d_ff_21_q, not_18_out);
  and and_46 (and_46_out, d_ff_22_q, not_18_out);
  and and_47 (and_47_out, d_ff_23_q, not_18_out);
  and and_48 (and_48_out, d_ff_24_q, not_18_out);
  and and_49 (and_49_out, d_ff_25_q, not_19_out);
  and and_50 (and_50_out, d_ff_26_q, not_19_out);
  and and_51 (and_51_out, d_ff_27_q, not_19_out);
  and and_52 (and_52_out, d_ff_28_q, not_19_out);
  and and_53 (and_53_out, d_ff_29_q, not_20_out);
  and and_54 (and_54_out, d_ff_30_q, not_20_out);
  and and_55 (and_55_out, d_ff_31_q, not_20_out);
  and and_56 (and_56_out, d_ff_32_q, not_20_out);
  D_Flip_Flop #(.trigger("falling")) d_ff_33 (.D(and_25_out), .clk(R0), .Q(d_ff_33_q));  // open: Qn, preset, reset
  D_Flip_Flop #(.trigger("falling")) d_ff_34 (.D(and_26_out), .clk(R0), .Q(d_ff_34_q));  // open: Qn, preset, reset
  D_Flip_Flop #(.trigger("falling")) d_ff_35 (.D(and_27_out), .clk(R0), .Q(d_ff_35_q));  // open: Qn, preset, reset
  D_Flip_Flop #(.trigger("falling")) d_ff_36 (
    .D(and_28_out), .clk(R0), .Q(d_ff_36_q), .reset(undriven));  // open: Qn, preset
  D_Flip_Flop #(.trigger("falling")) d_ff_37 (
    .D(and_29_out), .clk(R1), .Q(d_ff_37_q), .preset(undriven));  // open: Qn, reset
  D_Flip_Flop #(.trigger("falling")) d_ff_38 (.D(and_30_out), .clk(R1), .Q(d_ff_38_q));  // open: Qn, preset, reset
  D_Flip_Flop #(.trigger("falling")) d_ff_39 (.D(and_31_out), .clk(R1), .Q(d_ff_39_q));  // open: Qn, preset, reset
  D_Flip_Flop #(.trigger("falling")) d_ff_40 (
    .D(and_32_out), .clk(R1), .Q(d_ff_40_q), .reset(undriven_2));  // open: Qn, preset
  D_Flip_Flop #(.trigger("falling")) d_ff_41 (
    .D(and_33_out), .clk(R2), .Q(d_ff_41_q), .preset(undriven_2));  // open: Qn, reset
  D_Flip_Flop #(.trigger("falling")) d_ff_42 (.D(and_34_out), .clk(R2), .Q(d_ff_42_q));  // open: Qn, preset, reset
  D_Flip_Flop #(.trigger("falling")) d_ff_43 (.D(and_35_out), .clk(R2), .Q(d_ff_43_q));  // open: Qn, preset, reset
  D_Flip_Flop #(.trigger("falling")) d_ff_44 (.D(and_36_out), .clk(R2), .Q(d_ff_44_q));  // open: Qn, preset, reset
  D_Flip_Flop #(.trigger("falling")) d_ff_45 (.D(and_37_out), .clk(R3), .Q(d_ff_45_q));  // open: Qn, preset, reset
  D_Flip_Flop #(.trigger("falling")) d_ff_46 (.D(and_38_out), .clk(R3), .Q(d_ff_46_q));  // open: Qn, preset, reset
  D_Flip_Flop #(.trigger("falling")) d_ff_47 (.D(and_39_out), .clk(R3), .Q(d_ff_47_q));  // open: Qn, preset, reset
  D_Flip_Flop #(.trigger("falling")) d_ff_48 (.D(and_40_out), .clk(R3), .Q(d_ff_48_q));  // open: Qn, preset, reset
  D_Flip_Flop #(.trigger("falling")) d_ff_49 (.D(and_41_out), .clk(R4), .Q(d_ff_49_q));  // open: Qn, preset, reset
  D_Flip_Flop #(.trigger("falling")) d_ff_50 (.D(and_42_out), .clk(R4), .Q(d_ff_50_q));  // open: Qn, preset, reset
  D_Flip_Flop #(.trigger("falling")) d_ff_51 (.D(and_43_out), .clk(R4), .Q(d_ff_51_q));  // open: Qn, preset, reset
  D_Flip_Flop #(.trigger("falling")) d_ff_52 (.D(and_44_out), .clk(R4), .Q(d_ff_52_q));  // open: Qn, preset, reset
  D_Flip_Flop #(.trigger("falling")) d_ff_53 (.D(and_45_out), .clk(R5), .Q(d_ff_53_q));  // open: Qn, preset, reset
  D_Flip_Flop #(.trigger("falling")) d_ff_54 (.D(and_46_out), .clk(R5), .Q(d_ff_54_q));  // open: Qn, preset, reset
  D_Flip_Flop #(.trigger("falling")) d_ff_55 (.D(and_47_out), .clk(R5), .Q(d_ff_55_q));  // open: Qn, preset, reset
  D_Flip_Flop #(.trigger("falling")) d_ff_56 (.D(and_48_out), .clk(R5), .Q(d_ff_56_q));  // open: Qn, preset, reset
  D_Flip_Flop #(.trigger("falling")) d_ff_57 (.D(and_49_out), .clk(R6), .Q(d_ff_57_q));  // open: Qn, preset, reset
  D_Flip_Flop #(.trigger("falling")) d_ff_58 (.D(and_50_out), .clk(R6), .Q(d_ff_58_q));  // open: Qn, preset, reset
  D_Flip_Flop #(.trigger("falling")) d_ff_59 (.D(and_51_out), .clk(R6), .Q(d_ff_59_q));  // open: Qn, preset, reset
  D_Flip_Flop #(.trigger("falling")) d_ff_60 (.D(and_52_out), .clk(R6), .Q(d_ff_60_q));  // open: Qn, preset, reset
  D_Flip_Flop #(.trigger("falling")) d_ff_61 (.D(and_53_out), .clk(R7), .Q(d_ff_61_q));  // open: Qn, preset, reset
  D_Flip_Flop #(.trigger("falling")) d_ff_62 (.D(and_54_out), .clk(R7), .Q(d_ff_62_q));  // open: Qn, preset, reset
  D_Flip_Flop #(.trigger("falling")) d_ff_63 (.D(and_55_out), .clk(R7), .Q(d_ff_63_q));  // open: Qn, preset, reset
  D_Flip_Flop #(.trigger("falling")) d_ff_64 (.D(and_56_out), .clk(R7), .Q(d_ff_64_q));  // open: Qn, preset, reset
  and and_57 (d01, r0_t, d_ff_33_q);
  and and_58 (d02, r0_t, d_ff_34_q);
  and and_59 (d03, r0_t, d_ff_35_q);
  and and_60 (d04, r0_t, d_ff_36_q);
  and and_61 (d11, d_ff_37_q, r1_t);
  and and_62 (d12, d_ff_38_q, r1_t);
  and and_63 (d13, d_ff_39_q, r1_t);
  and and_64 (d14, d_ff_40_q, r1_t);
  and and_65 (d21, d_ff_41_q, r2_t);
  and and_66 (d22, d_ff_42_q, r2_t);
  and and_67 (d23, d_ff_43_q, r2_t);
  and and_68 (d24, d_ff_44_q, r2_t);
  and and_69 (d31, d_ff_45_q, r3_t);
  and and_70 (d32, d_ff_46_q, r3_t);
  and and_71 (d33, d_ff_47_q, r3_t);
  and and_72 (d34, d_ff_48_q, r3_t);
  and and_73 (d41, d_ff_49_q, r4_t);
  and and_74 (d42, d_ff_50_q, r4_t);
  and and_75 (d43, d_ff_51_q, r4_t);
  and and_76 (d44, d_ff_52_q, r4_t);
  and and_77 (d51, d_ff_53_q, r5_t);
  and and_78 (d52, d_ff_54_q, r5_t);
  and and_79 (d53, d_ff_55_q, r5_t);
  and and_80 (d54, d_ff_56_q, r5_t);
  and and_81 (d61, d_ff_57_q, r6_t);
  and and_82 (d62, d_ff_58_q, r6_t);
  and and_83 (d63, d_ff_59_q, r6_t);
  and and_84 (d64, d_ff_60_q, r6_t);
  and and_85 (d71, d_ff_61_q, r7_t);
  and and_86 (d72, d_ff_62_q, r7_t);
  and and_87 (d73, d_ff_63_q, r7_t);
  and and_88 (d74, d_ff_64_q, r7_t);
  or or_1 (DataOut4, d04, d14, d24, d34, d44, d54, d64, d74);
  or or_2 (DataOut1, d01, d11, d21, d31, d41, d51, d61, d71);
  or or_3 (DataOut2, d02, d12, d22, d32, d42, d52, d62, d72);
  or or_4 (DataOut3, d03, d13, d23, d33, d43, d53, d63, d73);

  // Other names for the same wires on the sheet: A1 = Address1; A2 = Address2; A3 = Address3; D1 = DataIn1;
  //   D2 = DataIn2; D3 = DataIn3; D4 = DataIn4; data1 = DataOut1; data2 = DataOut2; data3 = DataOut3;
  //   data4 = DataOut4; RW = R_W

  // Notes on the sheet:
  //   Ziming Dong  Student ID: 260951177
endmodule
