// Logisim project a6.circ as structural Verilog: 1 circuit, main circuit main
module main (
  input  l2,
  input  l3,
  input  in_3,
  input  in_4,
  input  in_5,
  input  in_6,
  input  in_7,
  input  l1,
  input  l4,
  output Negative,
  output Zero,
  output Overflow,
  output out_13,
  output out_14,
  output out_15,
  output out_16
);

  wire and_1_out, and_2_out, and_6_out, and_8_out, and_9_out, and_10_out, and_11_out, and_14_out, and_16_out,
       and_19_out, and_21_out, and_22_out, and_24_out, and_25_out, and_27_out, and_28_out, carry,
       clock_1_out, not_1_out, not_2_out, not_3_out, not_4_out, not_5_out, not_6_out, not_7_out, not_8_out,
       not_9_out, not_10_out, o1, o2, o3, o4, or_2_out, or_3_out, or_4_out, or_5_out, or_6_out, r1, r1a, r2,
       r2a, r3, r3a, r4, r4a, xor_1_out, xor_3_out, xor_4_out, xor_5_out, xor_7_out, xor_10_out, xor_11_out,
       xor_12_out, xor_13_out;

  Clock clock_1 (.out(clock_1_out));
  and and_1 (and_1_out, l1, r1);
  and and_2 (and_2_out, or_3_out, xor_1_out);
  or or_1 (carry, and_2_out, and_1_out);
  and and_3 (out_13, o1, clock_1_out);
  and and_4 (out_14, o2, clock_1_out);
  or or_2 (or_2_out, o2, o3, o4);
  xor xor_1 (xor_1_out, l1, r1);
  xor xor_2 (o1, or_3_out, xor_1_out);
  and and_5 (out_15, o3, clock_1_out);
  xor xor_3 (xor_3_out, o1, l1);
  xor xor_4 (xor_4_out, r1, o1);
  not not_1 (not_1_out, or_2_out);
  and and_6 (and_6_out, or_5_out, xor_5_out);
  or or_3 (or_3_out, and_6_out, and_10_out);
  and and_7 (out_16, o4, clock_1_out);
  and and_8 (and_8_out, xor_3_out, xor_4_out);
  and and_9 (and_9_out, o1, r1, in_7, not_1_out);
  and and_10 (and_10_out, l2, r2);
  xor xor_5 (xor_5_out, l2, r2);
  xor xor_6 (o2, or_5_out, xor_5_out);
  or or_4 (or_4_out, and_8_out, and_9_out);
  and and_11 (and_11_out, and_16_out, xor_7_out);
  or or_5 (or_5_out, and_11_out, and_14_out);
  and and_12 (Negative, clock_1_out, o1);
  and and_13 (Overflow, clock_1_out, or_4_out);
  and and_14 (and_14_out, l3, r3);
  or or_6 (or_6_out, o1, o2, o3, o4);
  xor xor_7 (xor_7_out, l3, r3);
  xor xor_8 (o3, and_16_out, xor_7_out);
  not not_2 (not_2_out, or_6_out);
  and and_15 (Zero, clock_1_out, not_2_out);
  and and_16 (and_16_out, l4, r4);
  xor xor_9 (o4, l4, r4);
  not not_3 (not_3_out, in_7);
  and and_17 (r1a, not_3_out, in_3);
  // AND_Gate and_18 has open pins: in0=not_4_out, in1=and_21_out, out=open
  and and_19 (and_19_out, in_3, in_7);
  not not_4 (not_4_out, and_19_out);
  xor xor_10 (xor_10_out, not_4_out, and_21_out);
  or or_7 (r1, xor_10_out, r1a);
  not not_5 (not_5_out, in_7);
  and and_20 (r2a, not_5_out, in_4);
  and and_21 (and_21_out, not_6_out, and_24_out);
  and and_22 (and_22_out, in_4, in_7);
  not not_6 (not_6_out, and_22_out);
  xor xor_11 (xor_11_out, not_6_out, and_24_out);
  or or_8 (r2, xor_11_out, r2a);
  not not_7 (not_7_out, in_7);
  and and_23 (r3a, not_7_out, in_5);
  and and_24 (and_24_out, not_8_out, and_27_out);
  and and_25 (and_25_out, in_5, in_7);
  not not_8 (not_8_out, and_25_out);
  xor xor_12 (xor_12_out, not_8_out, and_27_out);
  or or_9 (r3, xor_12_out, r3a);
  not not_9 (not_9_out, in_7);
  and and_26 (r4a, not_9_out, in_6);
  and and_27 (and_27_out, not_10_out, 1'b1);
  and and_28 (and_28_out, in_6, in_7);
  not not_10 (not_10_out, and_28_out);
  xor xor_13 (xor_13_out, 1'b1, not_10_out);
  or or_10 (r4, xor_13_out, r4a);

  // Other names for the same wires on the sheet: AS = in_7

  // Notes on the sheet:
  //   Ziming Dong
  //   Student ID: 260951177
endmodule
