// Logisim project a7.circ as structural Verilog: 18 circuits, main circuit main
module main (
  input  START,
  output Zero,
  output Negative,
  output Overflow,
  output Underflow
);

  wire addr_1_aout1, addr_1_aout2, addr_1_aout3, ALUmode, classicalalu_1_a1, classicalalu_1_a2,
       classicalalu_1_a3, classicalalu_1_a4, classicalram_1_d1out, classicalram_1_d2out,
       classicalram_1_d3out, classicalram_1_d4out, clock_1_out, cu_1_a1, cu_1_a2, cu_1_a3, cu_1_addrr,
       cu_1_addrw, cu_1_r1en, cu_1_r1w, cu_1_r2en, cu_1_r2w, ir_1_dataout1, ir_1_dataout2, ir_1_dataout3,
       ir_1_dataout4, IRw, l_1_dataout1, l_1_dataout2, l_1_dataout3, l_1_dataout4, Len, Lr, mar_1_aout1,
       mar_1_aout2, mar_1_aout3, MARw, mbr_1_dataout1, mbr_1_dataout2, mbr_1_dataout3, mbr_1_dataout4, MBRw,
       or_1_out, or_2_out, or_3_out, or_4_out, or_5_out, or_6_out, or_7_out, pc_1_a1, pc_1_a2, pc_1_a3,
       PCadd, PCr, r1_1_dataout1, r1_1_dataout2, r1_1_dataout3, r1_1_dataout4, r2_1_dataout1, r2_1_dataout2,
       r2_1_dataout3, r2_1_dataout4, r_1_dataout1, r_1_dataout2, r_1_dataout3, r_1_dataout4, RAMr, RAMw, Ren,
       Rr;

  Clock clock_1 (.out(clock_1_out));
  MAR mar_1 (
    .aOut1(mar_1_aout1), .aOut2(mar_1_aout2), .aOut3(mar_1_aout3), .CLK(clock_1_out), .MARw(MARw),
    .aIn1(or_1_out), .aIn2(or_2_out), .aIn3(or_3_out));
  ClassicalRAM classicalram_1 (
    .D1out(classicalram_1_d1out), .D2out(classicalram_1_d2out), .D3out(classicalram_1_d3out),
    .D4out(classicalram_1_d4out), .A3(mar_1_aout1), .CLK(clock_1_out), .Mode(RAMw), .RAMread(RAMr),
    .D1in(classicalram_1_d1out), .D2in(classicalram_1_d2out), .A1(mar_1_aout3), .D3in(classicalram_1_d3out),
    .D4in(classicalram_1_d4out), .A2(mar_1_aout2));
  or or_1 (or_1_out, addr_1_aout1, pc_1_a1);
  or or_2 (or_2_out, addr_1_aout2, pc_1_a2);
  or or_3 (or_3_out, addr_1_aout3, pc_1_a3);
  MBR mbr_1 (
    .dataIn1(classicalram_1_d1out), .dataIn2(classicalram_1_d2out), .dataIn3(classicalram_1_d3out),
    .dataIn4(classicalram_1_d4out), .MBRw(MBRw), .CLK(clock_1_out), .dataOut1(mbr_1_dataout1),
    .dataOut2(mbr_1_dataout2), .dataOut3(mbr_1_dataout3), .dataOut4(mbr_1_dataout4));
  or or_4 (or_4_out, classicalalu_1_a4, r2_1_dataout4, r1_1_dataout4, classicalram_1_d4out);
  or or_5 (or_5_out, r1_1_dataout3, r2_1_dataout3, classicalalu_1_a3, classicalram_1_d3out);
  or or_6 (or_6_out, r1_1_dataout2, r2_1_dataout2, classicalalu_1_a2, classicalram_1_d2out);
  or or_7 (or_7_out, r1_1_dataout1, r2_1_dataout1, classicalalu_1_a1, classicalram_1_d1out);
  PC pc_1 (.PCread(PCr), .CLK(clock_1_out), .START(START), .PCadd(PCadd), .a3(pc_1_a3), .a2(pc_1_a2), .a1(pc_1_a1));
  IR ir_1 (
    .dataIn1(mbr_1_dataout1), .dataIn2(mbr_1_dataout2), .dataIn3(mbr_1_dataout3), .dataIn4(mbr_1_dataout4),
    .IRw(IRw), .CLK(clock_1_out), .dataOut1(ir_1_dataout1), .dataOut2(ir_1_dataout2),
    .dataOut3(ir_1_dataout3), .dataOut4(ir_1_dataout4));
  ADDR addr_1 (
    .aIn1(cu_1_a1), .aIn2(cu_1_a2), .aIn3(cu_1_a3), .CLK(clock_1_out), .AddrW(cu_1_addrw),
    .AddrR(cu_1_addrr), .aOut1(addr_1_aout1), .aOut2(addr_1_aout2), .aOut3(addr_1_aout3));
  R1 r1_1 (
    .dataIn4(or_4_out), .dataIn3(or_5_out), .dataIn2(or_6_out), .dataIn1(or_7_out), .en(cu_1_r1en),
    .R1w(cu_1_r1w), .CLK(clock_1_out), .dataOut4(r1_1_dataout4), .dataOut3(r1_1_dataout3),
    .dataOut2(r1_1_dataout2), .dataOut1(r1_1_dataout1));
  L l_1 (
    .dataIn4(or_4_out), .dataIn3(or_5_out), .dataIn2(or_6_out), .dataIn1(or_7_out), .Lr(Lr), .Len(Len),
    .CLK(clock_1_out), .dataOut4(l_1_dataout4), .dataOut3(l_1_dataout3), .dataOut2(l_1_dataout2),
    .dataOut1(l_1_dataout1));
  ClassicalALU classicalalu_1 (
    .L1(l_1_dataout1), .L2(l_1_dataout2), .L3(l_1_dataout3), .L4(l_1_dataout4), .R1(r_1_dataout1),
    .R2(r_1_dataout2), .R3(r_1_dataout3), .R4(r_1_dataout4), .CLK(clock_1_out), .mode(ALUmode), .Zero(Zero),
    .Negative(Negative), .Overflow(Overflow), .Underflow(Underflow), .A1(classicalalu_1_a1),
    .A2(classicalalu_1_a2), .A3(classicalalu_1_a3), .A4(classicalalu_1_a4));
  CU cu_1 (
    .CLK(clock_1_out), .Ir1(ir_1_dataout1), .Ir2(ir_1_dataout2), .lr3(ir_1_dataout3), .lr4(ir_1_dataout4),
    .START(START), .a3(cu_1_a3), .a2(cu_1_a2), .a1(cu_1_a1), .MARw(MARw), .ALUmode(ALUmode), .MBRw(MBRw),
    .Len(Len), .IRw(IRw), .Lr(Lr), .Ren(Ren), .PCadd(PCadd), .PCr(PCr), .Rr(Rr), .R1w(cu_1_r1w),
    .ADDRr(cu_1_addrr), .R1en(cu_1_r1en), .ADDRw(cu_1_addrw), .R2w(cu_1_r2w), .R2en(cu_1_r2en), .RAMen(RAMr),
    .RAMw(RAMw));
  R2 r2_1 (
    .dataIn4(or_4_out), .dataIn3(or_5_out), .dataIn2(or_6_out), .dataIn1(or_7_out), .en(cu_1_r2en),
    .R2w(cu_1_r2w), .CLK(clock_1_out), .dataOut4(r2_1_dataout4), .dataOut3(r2_1_dataout3),
    .dataOut2(r2_1_dataout2), .dataOut1(r2_1_dataout1));
  R r_1 (
    .dataIn4(or_4_out), .dataIn3(or_5_out), .dataIn2(or_6_out), .dataIn1(or_7_out), .Rr(Rr), .Ren(Ren),
    .CLK(clock_1_out), .dataOut4(r_1_dataout4), .dataOut3(r_1_dataout3), .dataOut2(r_1_dataout2),
    .dataOut1(r_1_dataout1));

  // Notes on the sheet:
  //   ZIming Dong
  //   ID: 260951177
  //   START BUTTON IS BELOW
  //   Click it twice before testing start
  //   Click START twice before test
  //   SInce our address start at 010
endmodule

module ClassicalRAM (
  input  CLK,
  input  A1,
  input  A2,
  input  A3,
  input  Mode,
  input  RAMread,
  input  D1in,
  input  D2in,
  input  D3in,
  input  D4in,
  output D1out,
  output D2out,
  output D3out,
  output D4out
);

  wire and_1_out, and_2_out, and_3_out, and_4_out, and_5_out, and_6_out, and_7_out, and_8_out, and_9_out,
       and_10_out, and_11_out, and_12_out, and_13_out, and_14_out, and_15_out, and_16_out, and_17_out,
       and_18_out, and_19_out, and_20_out, and_21_out, and_22_out, and_23_out, and_24_out, and_25_out,
       and_26_out, and_27_out, and_28_out, and_29_out, and_30_out, and_31_out, and_32_out, and_33_out,
       and_34_out, and_35_out, and_36_out, and_37_out, and_38_out, and_39_out, and_40_out, and_41_out,
       and_42_out, and_43_out, and_44_out, and_45_out, and_46_out, and_47_out, and_48_out, and_49_out,
       and_50_out, and_51_out, and_52_out, and_53_out, and_54_out, and_55_out, and_56_out, and_57_out,
       and_58_out, and_59_out, and_60_out, and_61_out, and_62_out, and_63_out, and_64_out, and_65_out,
       and_66_out, and_67_out, and_68_out, and_69_out, and_70_out, and_71_out, and_72_out, and_73_out,
       and_74_out, and_75_out, and_76_out, and_77_out, and_78_out, and_79_out, and_80_out, d_ff_1_q,
       d_ff_2_q, d_ff_3_q, d_ff_4_q, d_ff_5_q, d_ff_6_q, d_ff_7_q, d_ff_8_q, d_ff_9_q, d_ff_10_q, d_ff_11_q,
       d_ff_12_q, d_ff_13_q, d_ff_14_q, d_ff_15_q, d_ff_16_q, d_ff_17_q, d_ff_18_q, d_ff_19_q, d_ff_20_q,
       d_ff_21_q, d_ff_22_q, d_ff_23_q, d_ff_24_q, d_ff_25_q, d_ff_26_q, d_ff_27_q, d_ff_28_q, d_ff_29_q,
       d_ff_30_q, d_ff_31_q, d_ff_32_q, not_1_out, not_2_out, not_3_out, not_4_out, not_5_out, not_6_out,
       not_7_out, not_8_out, not_9_out, not_10_out, not_11_out, not_12_out;

  not not_1 (not_1_out, A3);
  not not_2 (not_2_out, A2);
  not not_3 (not_3_out, A2);
  not not_4 (not_4_out, A3);
  not not_5 (not_5_out, A1);
  not not_6 (not_6_out, A1);
  not not_7 (not_7_out, A3);
  not not_8 (not_8_out, A1);
  not not_9 (not_9_out, A2);
  not not_10 (not_10_out, A1);
  not not_11 (not_11_out, A2);
  not not_12 (not_12_out, A3);
  and and_1 (and_1_out, A1, A2, CLK, A3);
  and and_2 (and_2_out, and_1_out, Mode);
  and and_3 (and_3_out, A1, A2, CLK, not_1_out);
  and and_4 (and_4_out, and_3_out, Mode);
  and and_5 (and_5_out, A1, not_2_out, CLK, A3);
  and and_6 (and_6_out, and_5_out, Mode);
  and and_7 (and_7_out, A1, not_3_out, CLK, not_4_out);
  and and_8 (and_8_out, and_7_out, Mode);
  and and_9 (and_9_out, not_5_out, A2, CLK, A3);
  and and_10 (and_10_out, and_9_out, Mode);
  and and_11 (and_11_out, not_6_out, A2, CLK, not_7_out);
  and and_12 (and_12_out, and_11_out, Mode);
  and and_13 (and_13_out, not_8_out, not_9_out, CLK, A3);
  and and_14 (and_14_out, and_13_out, Mode);
  and and_15 (and_15_out, not_10_out, not_11_out, CLK, not_12_out);
  and and_16 (and_16_out, and_15_out, Mode);
  and and_17 (and_17_out, and_1_out, Mode, D1in);
  D_Flip_Flop #(.trigger("high")) d_ff_1 (.D(and_17_out), .clk(and_2_out), .Q(d_ff_1_q));  // open: Qn, preset, reset
  and and_18 (and_18_out, and_3_out, Mode, D1in);
  D_Flip_Flop #(.trigger("high")) d_ff_2 (.D(and_18_out), .clk(and_4_out), .Q(d_ff_2_q));  // open: Qn, preset, reset
  and and_19 (and_19_out, and_5_out, Mode, D1in);
  D_Flip_Flop #(.trigger("high")) d_ff_3 (.D(and_19_out), .clk(and_6_out), .Q(d_ff_3_q));  // open: Qn, preset, reset
  and and_20 (and_20_out, and_7_out, Mode, D1in);
  D_Flip_Flop #(.trigger("high")) d_ff_4 (.D(and_20_out), .clk(and_8_out), .Q(d_ff_4_q));  // open: Qn, preset, reset
  and and_21 (and_21_out, and_9_out, Mode, D1in);
  D_Flip_Flop #(.trigger("high")) d_ff_5 (.D(and_21_out), .clk(and_10_out), .Q(d_ff_5_q));  // open: Qn, preset, reset
  and and_22 (and_22_out, and_11_out, Mode, D1in);
  D_Flip_Flop #(.trigger("high")) d_ff_6 (.D(and_22_out), .clk(and_12_out), .Q(d_ff_6_q));  // open: Qn, preset, reset
  and and_23 (and_23_out, and_13_out, Mode, D1in);
  D_Flip_Flop #(.trigger("high")) d_ff_7 (.D(and_23_out), .clk(and_14_out), .Q(d_ff_7_q));  // open: Qn, preset, reset
  and and_24 (and_24_out, and_15_out, Mode, D1in);
  D_Flip_Flop #(.trigger("high")) d_ff_8 (.D(and_24_out), .clk(and_16_out), .Q(d_ff_8_q));  // open: Qn, preset, reset
  or or_1 (D1out, and_25_out, and_26_out, and_27_out, and_28_out, and_29_out, and_30_out, and_31_out, and_32_out);
  and and_25 (and_25_out, d_ff_1_q, and_1_out, RAMread);
  and and_26 (and_26_out, d_ff_2_q, and_3_out, RAMread);
  and and_27 (and_27_out, d_ff_3_q, and_5_out, RAMread);
  and and_28 (and_28_out, d_ff_4_q, and_7_out, RAMread);
  and and_29 (and_29_out, d_ff_5_q, and_9_out, RAMread);
  and and_30 (and_30_out, d_ff_6_q, and_11_out, RAMread);
  and and_31 (and_31_out, d_ff_7_q, and_13_out, RAMread);
  and and_32 (and_32_out, d_ff_8_q, and_15_out, RAMread);
  and and_33 (and_33_out, and_1_out, Mode, D2in);
  D_Flip_Flop #(.trigger("high")) d_ff_9 (.D(and_33_out), .clk(and_2_out), .Q(d_ff_9_q));  // open: Qn, preset, reset
  and and_34 (and_34_out, and_3_out, Mode, D2in);
  D_Flip_Flop #(.trigger("high")) d_ff_10 (.D(and_34_out), .clk(and_4_out), .Q(d_ff_10_q));  // open: Qn, preset, reset
  and and_35 (and_35_out, and_5_out, Mode, D2in);
  D_Flip_Flop #(.trigger("high")) d_ff_11 (.D(and_35_out), .clk(and_6_out), .Q(d_ff_11_q));  // open: Qn, preset, reset
  and and_36 (and_36_out, and_7_out, Mode, D2in);
  D_Flip_Flop #(.trigger("high")) d_ff_12 (.D(and_36_out), .clk(and_8_out), .Q(d_ff_12_q));  // open: Qn, preset, reset
  and and_37 (and_37_out, and_9_out, Mode, D2in);
  D_Flip_Flop #(.trigger("high")) d_ff_13 (.D(and_37_out), .clk(and_10_out), .Q(d_ff_13_q));  // open: Qn, preset, reset
  and and_38 (and_38_out, and_11_out, Mode, D2in);
  D_Flip_Flop #(.trigger("high")) d_ff_14 (.D(and_38_out), .clk(and_12_out), .Q(d_ff_14_q));  // open: Qn, preset, reset
  and and_39 (and_39_out, and_13_out, Mode, D2in);
  D_Flip_Flop #(.trigger("high")) d_ff_15 (.D(and_39_out), .clk(and_14_out), .Q(d_ff_15_q));  // open: Qn, preset, reset
  and and_40 (and_40_out, and_15_out, Mode, D2in);
  D_Flip_Flop #(.trigger("high")) d_ff_16 (.D(and_40_out), .clk(and_16_out), .Q(d_ff_16_q));  // open: Qn, preset, reset
  or or_2 (D2out, and_41_out, and_42_out, and_43_out, and_44_out, and_45_out, and_46_out, and_47_out, and_48_out);
  and and_41 (and_41_out, d_ff_9_q, and_1_out, RAMread);
  and and_42 (and_42_out, d_ff_10_q, and_3_out, RAMread);
  and and_43 (and_43_out, d_ff_11_q, and_5_out, RAMread);
  and and_44 (and_44_out, d_ff_12_q, and_7_out, RAMread);
  and and_45 (and_45_out, d_ff_13_q, and_9_out, RAMread);
  and and_46 (and_46_out, d_ff_14_q, and_11_out, RAMread);
  and and_47 (and_47_out, d_ff_15_q, and_13_out, RAMread);
  and and_48 (and_48_out, d_ff_16_q, and_15_out, RAMread);
  Clock clock_1 ();  // open: out
  and and_49 (and_49_out, and_1_out, Mode, D3in);
  and and_50 (and_50_out, and_3_out, Mode, D3in);
  and and_51 (and_51_out, and_5_out, Mode, D3in);
  and and_52 (and_52_out, and_7_out, Mode, D3in);
  and and_53 (and_53_out, and_9_out, Mode, D3in);
  and and_54 (and_54_out, and_11_out, Mode, D3in);
  and and_55 (and_55_out, and_13_out, Mode, D3in);
  and and_56 (and_56_out, and_15_out, Mode, D3in);
  D_Flip_Flop #(.trigger("high")) d_ff_17 (.D(and_49_out), .clk(and_2_out), .Q(d_ff_17_q));  // open: Qn, preset, reset
  D_Flip_Flop #(.trigger("high")) d_ff_18 (.D(and_50_out), .clk(and_4_out), .Q(d_ff_18_q));  // open: Qn, preset, reset
  D_Flip_Flop #(.trigger("high")) d_ff_19 (.D(and_51_out), .clk(and_6_out), .Q(d_ff_19_q));  // open: Qn, preset, reset
  D_Flip_Flop #(.trigger("high")) d_ff_20 (.D(and_52_out), .clk(and_8_out), .Q(d_ff_20_q));  // open: Qn, preset, reset
  D_Flip_Flop #(.trigger("high")) d_ff_21 (.D(and_53_out), .clk(and_10_out), .Q(d_ff_21_q));  // open: Qn, preset, reset
  D_Flip_Flop #(.trigger("high")) d_ff_22 (.D(and_54_out), .clk(and_12_out), .Q(d_ff_22_q));  // open: Qn, preset, reset
  D_Flip_Flop #(.trigger("high")) d_ff_23 (.D(and_55_out), .clk(and_14_out), .Q(d_ff_23_q));  // open: Qn, preset, reset
  D_Flip_Flop #(.trigger("high")) d_ff_24 (.D(and_56_out), .clk(and_16_out), .Q(d_ff_24_q));  // open: Qn, preset, reset
  or or_3 (D3out, and_57_out, and_58_out, and_59_out, and_60_out, and_61_out, and_62_out, and_63_out, and_64_out);
  and and_57 (and_57_out, d_ff_17_q, and_1_out, RAMread);
  and and_58 (and_58_out, d_ff_18_q, and_3_out, RAMread);
  and and_59 (and_59_out, d_ff_19_q, and_5_out, RAMread);
  and and_60 (and_60_out, d_ff_20_q, and_7_out, RAMread);
  and and_61 (and_61_out, d_ff_21_q, and_9_out, RAMread);
  and and_62 (and_62_out, d_ff_22_q, and_11_out, RAMread);
  and and_63 (and_63_out, d_ff_23_q, and_13_out, RAMread);
  and and_64 (and_64_out, d_ff_24_q, and_15_out, RAMread);
  and and_65 (and_65_out, and_1_out, Mode, D4in);
  D_Flip_Flop #(.trigger("high")) d_ff_25 (.D(and_65_out), .clk(and_2_out), .Q(d_ff_25_q));  // open: Qn, preset, reset
  and and_66 (and_66_out, and_3_out, Mode, D4in);
  D_Flip_Flop #(.trigger("high")) d_ff_26 (.D(and_66_out), .clk(and_4_out), .Q(d_ff_26_q));  // open: Qn, preset, reset
  and and_67 (and_67_out, and_5_out, Mode, D4in);
  D_Flip_Flop #(.trigger("high")) d_ff_27 (.D(and_67_out), .clk(and_6_out), .Q(d_ff_27_q));  // open: Qn, preset, reset
  and and_68 (and_68_out, and_7_out, Mode, D4in);
  D_Flip_Flop #(.trigger("high")) d_ff_28 (.D(and_68_out), .clk(and_8_out), .Q(d_ff_28_q));  // open: Qn, preset, reset
  and and_69 (and_69_out, and_9_out, Mode, D4in);
  D_Flip_Flop #(.trigger("high")) d_ff_29 (.D(and_69_out), .clk(and_10_out), .Q(d_ff_29_q));  // open: Qn, preset, reset
  and and_70 (and_70_out, and_11_out, Mode, D4in);
  D_Flip_Flop #(.trigger("high")) d_ff_30 (.D(and_70_out), .clk(and_12_out), .Q(d_ff_30_q));  // open: Qn, preset, reset
  and and_71 (and_71_out, and_13_out, Mode, D4in);
  D_Flip_Flop #(.trigger("high")) d_ff_31 (.D(and_71_out), .clk(and_14_out), .Q(d_ff_31_q));  // open: Qn, preset, reset
  and and_72 (and_72_out, and_15_out, Mode, D4in);
  D_Flip_Flop #(.trigger("high")) d_ff_32 (.D(and_72_out), .clk(and_16_out), .Q(d_ff_32_q));  // open: Qn, preset, reset
  or or_4 (D4out, and_73_out, and_74_out, and_75_out, and_76_out, and_77_out, and_78_out, and_79_out, and_80_out);
  and and_73 (and_73_out, d_ff_25_q, and_1_out, RAMread);
  and and_74 (and_74_out, d_ff_26_q, and_3_out, RAMread);
  and and_75 (and_75_out, d_ff_27_q, and_5_out, RAMread);
  and and_76 (and_76_out, d_ff_28_q, and_7_out, RAMread);
  and and_77 (and_77_out, d_ff_29_q, and_9_out, RAMread);
  and and_78 (and_78_out, d_ff_30_q, and_11_out, RAMread);
  and and_79 (and_79_out, d_ff_31_q, and_13_out, RAMread);
  and and_80 (and_80_out, d_ff_32_q, and_15_out, RAMread);

  // Notes on the sheet:
  //   3-bit address input pins
  //   Mode input pin
  //   4-bit data input pins
  //   4-bit data output pins
endmodule

module ClassicalALU (
  input  L1,
  input  L2,
  input  L3,
  input  L4,
  input  R1,
  input  R2,
  input  R3,
  input  R4,
  input  CLK,
  input  mode,
  output Zero,
  output Negative,
  output Overflow,
  output Underflow,
  output A1,
  output A2,
  output A3,
  output A4
);

  wire and_1_out, and_2_out, and_3_out, and_4_out, and_5_out, and_6_out, and_7_out, and_8_out, and_9_out,
       and_10_out, and_11_out, and_12_out, and_13_out, and_14_out, and_15_out, and_16_out, and_17_out,
       and_18_out, and_19_out, and_20_out, and_21_out, and_22_out, and_24_out, and_25_out, and_26_out,
       and_27_out, filladder_1_c, filladder_2_c, filladder_3_c, Neg_out, not_1_out, not_2_out, not_3_out,
       not_4_out, not_5_out, not_6_out, not_7_out, not_8_out, not_9_out, not_10_out, not_11_out, not_12_out,
       not_13_out, not_14_out, not_15_out, or_1_out, or_2_out, or_3_out, or_4_out, or_5_out, Pos_out,
       xor_2_out, xor_3_out, xor_4_out, xor_5_out;

  not not_1 (not_1_out, mode);
  and and_1 (and_1_out, L1, CLK);
  and and_2 (and_2_out, L2, CLK);
  and and_3 (and_3_out, L3, CLK);
  FillAdder filladder_1 (.A(or_1_out), .B(and_1_out), .Carry(filladder_2_c), .C(filladder_1_c), .Sum(A1));
  and and_4 (and_4_out, L4, CLK);
  FillAdder filladder_2 (.A(or_2_out), .B(and_2_out), .Carry(filladder_3_c), .C(filladder_2_c), .Sum(A2));
  or or_1 (or_1_out, xor_2_out, and_6_out);
  FillAdder filladder_3 (.A(or_3_out), .B(and_3_out), .Carry(and_5_out), .C(filladder_3_c), .Sum(A3));
  or or_2 (or_2_out, xor_3_out, and_8_out);
  or or_3 (or_3_out, xor_4_out, and_9_out);
  and and_5 (and_5_out, and_4_out, or_4_out);
  xor xor_1 (A4, and_4_out, or_4_out);
  and and_6 (and_6_out, and_12_out, not_1_out);
  and and_7 (and_7_out, not_6_out, and_10_out);
  or or_4 (or_4_out, xor_5_out, and_14_out);
  not not_2 (not_2_out, A4);
  not not_3 (not_3_out, A3);
  not not_4 (not_4_out, A2);
  not not_5 (not_5_out, A1);
  and and_8 (and_8_out, and_13_out, not_1_out);
  and and_9 (and_9_out, and_17_out, not_1_out);
  xor xor_2 (xor_2_out, not_6_out, and_10_out);
  and and_10 (and_10_out, not_10_out, and_16_out);
  and and_11 (and_11_out, not_2_out, not_3_out, not_4_out, not_5_out);
  and and_12 (and_12_out, R1, CLK);
  and and_13 (and_13_out, R2, CLK);
  and and_14 (and_14_out, and_18_out, not_1_out);
  and and_15 (and_15_out, and_12_out, mode);
  not not_6 (not_6_out, and_15_out);
  xor xor_3 (xor_3_out, not_10_out, and_16_out);
  and and_16 (and_16_out, not_11_out, and_22_out);
  not not_7 (not_7_out, or_1_out);
  not not_8 (not_8_out, and_1_out);
  not not_9 (not_9_out, or_1_out);
  and and_17 (and_17_out, R3, CLK);
  and and_18 (and_18_out, R4, CLK);
  and and_19 (and_19_out, and_13_out, mode);
  and and_20 (and_20_out, and_17_out, mode);
  and and_21 (and_21_out, and_18_out, mode);
  not not_10 (not_10_out, and_19_out);
  not not_11 (not_11_out, and_20_out);
  not not_12 (not_12_out, and_21_out);
  xor xor_4 (xor_4_out, not_11_out, and_22_out);
  and and_22 (and_22_out, not_12_out, 1'b1);
  and Neg (Neg_out, or_1_out, and_1_out);
  and Pos (Pos_out, not_7_out, not_8_out);
  and and_23 (Zero, and_11_out, CLK);
  xor xor_5 (xor_5_out, not_12_out, 1'b1);
  and and_24 (and_24_out, A1, Neg_out);
  and and_25 (and_25_out, Pos_out, A1);
  and and_26 (and_26_out, not_13_out, not_9_out, filladder_1_c);
  not not_13 (not_13_out, mode);
  not not_14 (not_14_out, filladder_1_c);
  and and_27 (and_27_out, and_24_out, not_14_out);
  or or_5 (or_5_out, and_26_out, and_25_out, and_27_out);
  not not_15 (not_15_out, Zero);
  and notZero (Overflow, or_5_out, not_15_out);
  and and_28 (Underflow, Overflow, A1);

  assign Negative = A1;

  // Other names for the same wires on the sheet: CMD = mode

  // Notes on the sheet:
  //   Add/Sub command
  //   0 add, 1 sub
  //   B Input
  //   L input
  //   A-out output
  //   A Input
  //   Adder
  //   R Input
  //   2's Complement
  //   Status output
  //   -8 + -8 is underflow (not supported)
endmodule

module FillAdder (
  input  A,
  input  B,
  input  Carry,
  output C,
  output Sum
);

  wire and_1_out, and_2_out, xor_1_out;

  and and_1 (and_1_out, A, B);
  xor xor_1 (xor_1_out, A, B);
  and and_2 (and_2_out, xor_1_out, Carry);
  or or_1 (C, and_1_out, and_2_out);
  xor xor_2 (Sum, xor_1_out, Carry);
endmodule

module CU (
  input  CLK,
  input  Ir1,
  input  Ir2,
  input  lr3,
  input  lr4,
  input  START,
  output a3,
  output a2,
  output a1,
  output MARw,
  output ALUmode,
  output MBRw,
  output Len,
  output IRw,
  output Lr,
  output Ren,
  output PCadd,
  output PCr,
  output Rr,
  output R1w,
  output ADDRr,
  output R1en,
  output ADDRw,
  output R2w,
  output R2en,
  output RAMen,
  output RAMw
);

  wire divide_1_add, divide_1_ld, divide_1_sub, divide_1_sv;

  divide divide_1 (
    .CLK(CLK), .Ir1(Ir1), .Ir2(Ir2), .LD(divide_1_ld), .SV(divide_1_sv), .ADD(divide_1_add),
    .SUB(divide_1_sub));
  IC ic_1 (
    .Load(divide_1_ld), .Save(divide_1_sv), .Add(divide_1_add), .Sub(divide_1_sub), .Ir3(lr3), .Ir4(lr4),
    .CLK(CLK), .START(START), .a3(a3), .a2(a2), .a1(a1), .MARw(MARw), .ALUmode(ALUmode), .MBRw(MBRw),
    .Len(Len), .IRw(IRw), .Lr(Lr), .Ren(Ren), .PCadd(PCadd), .PCr(PCr), .Rr(Rr), .R1w(R1w), .ADDRr(ADDRr),
    .R1en(R1en), .ADDRw(ADDRw), .R2w(R2w), .R2en(R2en), .RAMen(RAMen), .RAMw(RAMw));
endmodule

module MAR (
  input  aIn1,
  input  aIn2,
  input  aIn3,
  input  CLK,
  input  MARw,
  output aOut1,
  output aOut2,
  output aOut3
);

  wire and_1_out, d_ff_1_q, d_ff_2_q, d_ff_3_q, not_1_out;

  and and_1 (and_1_out, CLK, MARw);
  not not_1 (not_1_out, MARw);
  D_Flip_Flop #(.trigger("falling")) d_ff_1 (.D(aIn1), .clk(and_1_out), .Q(d_ff_1_q));  // open: Qn, preset, reset
  D_Flip_Flop #(.trigger("falling")) d_ff_2 (.D(aIn2), .clk(and_1_out), .Q(d_ff_2_q));  // open: Qn, preset, reset
  D_Flip_Flop #(.trigger("falling")) d_ff_3 (.D(aIn3), .clk(and_1_out), .Q(d_ff_3_q));  // open: Qn, preset, reset
  and and_2 (aOut1, d_ff_1_q, not_1_out);
  and and_3 (aOut2, d_ff_2_q, not_1_out);
  and and_4 (aOut3, d_ff_3_q, not_1_out);
endmodule

module MBR (
  input  dataIn1,
  input  dataIn2,
  input  dataIn3,
  input  dataIn4,
  input  MBRw,
  input  CLK,
  output dataOut1,
  output dataOut2,
  output dataOut3,
  output dataOut4
);

  wire and_1_out, d_ff_1_q, d_ff_2_q, d_ff_3_q, d_ff_4_q, not_1_out;

  not not_1 (not_1_out, MBRw);
  and and_1 (and_1_out, MBRw, CLK);
  D_Flip_Flop #(.trigger("falling")) d_ff_1 (.D(dataIn1), .clk(and_1_out), .Q(d_ff_1_q));  // open: Qn, preset, reset
  D_Flip_Flop #(.trigger("falling")) d_ff_2 (.D(dataIn2), .clk(and_1_out), .Q(d_ff_2_q));  // open: Qn, preset, reset
  D_Flip_Flop #(.trigger("falling")) d_ff_3 (.D(dataIn3), .clk(and_1_out), .Q(d_ff_3_q));  // open: Qn, preset, reset
  D_Flip_Flop #(.trigger("falling")) d_ff_4 (.D(dataIn4), .clk(and_1_out), .Q(d_ff_4_q));  // open: Qn, preset, reset
  and and_2 (dataOut1, d_ff_1_q, not_1_out);
  and and_3 (dataOut2, d_ff_2_q, not_1_out);
  and and_4 (dataOut3, d_ff_3_q, not_1_out);
  and and_5 (dataOut4, d_ff_4_q, not_1_out);
endmodule

module PC (
  input  PCread,
  input  CLK,
  input  START,
  input  PCadd,
  output a3,
  output a2,
  output a1
);

  wire and_1_out, d_ff_1_q, d_ff_2_q, d_ff_3_q, increment_1_a1out, increment_1_a2out, increment_1_a3out;

  and and_1 (and_1_out, CLK, PCadd);
  D_Flip_Flop d_ff_1 (.D(increment_1_a1out), .clk(and_1_out), .Q(d_ff_1_q), .reset(START));  // open: Qn, preset
  D_Flip_Flop d_ff_2 (.D(increment_1_a2out), .clk(and_1_out), .Q(d_ff_2_q), .reset(START));  // open: Qn, preset
  D_Flip_Flop d_ff_3 (.D(increment_1_a3out), .clk(and_1_out), .Q(d_ff_3_q), .preset(START));  // open: Qn, reset
  Increment increment_1 (
    .a3In(d_ff_3_q), .a2In(d_ff_2_q), .a1In(d_ff_1_q), .a3Out(increment_1_a3out), .a2Out(increment_1_a2out),
    .a1Out(increment_1_a1out));
  and and_2 (a3, d_ff_1_q, PCread);
  and and_3 (a2, d_ff_2_q, PCread);
  and and_4 (a1, d_ff_3_q, PCread);
endmodule

module ADDR (
  input  aIn1,
  input  aIn2,
  input  aIn3,
  input  CLK,
  input  AddrW,
  input  AddrR,
  output aOut1,
  output aOut2,
  output aOut3
);

  wire and_1_out, d_ff_1_q, d_ff_2_q, d_ff_3_q;

  and and_1 (and_1_out, CLK, AddrW);
  D_Flip_Flop #(.trigger("falling")) d_ff_1 (.D(aIn1), .clk(and_1_out), .Q(d_ff_1_q));  // open: Qn, preset, reset
  D_Flip_Flop #(.trigger("falling")) d_ff_2 (.D(aIn2), .clk(and_1_out), .Q(d_ff_2_q));  // open: Qn, preset, reset
  D_Flip_Flop #(.trigger("falling")) d_ff_3 (.D(aIn3), .clk(and_1_out), .Q(d_ff_3_q));  // open: Qn, preset, reset
  and and_2 (aOut1, d_ff_1_q, AddrR);
  and and_3 (aOut2, d_ff_2_q, AddrR);
  and and_4 (aOut3, d_ff_3_q, AddrR);
endmodule

module IR (
  input  dataIn1,
  input  dataIn2,
  input  dataIn3,
  input  dataIn4,
  input  IRw,
  input  CLK,
  output dataOut1,
  output dataOut2,
  output dataOut3,
  output dataOut4
);

  wire and_1_out, d_ff_1_q, d_ff_2_q, d_ff_3_q, d_ff_4_q, not_1_out;

  and and_1 (and_1_out, IRw, CLK);
  not not_1 (not_1_out, IRw);
  D_Flip_Flop #(.trigger("falling")) d_ff_1 (.D(dataIn1), .clk(and_1_out), .Q(d_ff_1_q));  // open: Qn, preset, reset
  D_Flip_Flop #(.trigger("falling")) d_ff_2 (.D(dataIn2), .clk(and_1_out), .Q(d_ff_2_q));  // open: Qn, preset, reset
  D_Flip_Flop #(.trigger("falling")) d_ff_3 (.D(dataIn3), .clk(and_1_out), .Q(d_ff_3_q));  // open: Qn, preset, reset
  D_Flip_Flop #(.trigger("falling")) d_ff_4 (.D(dataIn4), .clk(and_1_out), .Q(d_ff_4_q));  // open: Qn, preset, reset
  and and_2 (dataOut1, d_ff_1_q, not_1_out);
  and and_3 (dataOut2, d_ff_2_q, not_1_out);
  and and_4 (dataOut3, d_ff_3_q, not_1_out);
  and and_5 (dataOut4, d_ff_4_q, not_1_out);
endmodule

module R1 (
  input  dataIn4,
  input  dataIn3,
  input  dataIn2,
  input  dataIn1,
  input  en,
  input  R1w,
  input  CLK,
  output dataOut4,
  output dataOut3,
  output dataOut2,
  output dataOut1
);

  wire and_1_out, d_ff_1_q, d_ff_2_q, d_ff_3_q, d_ff_4_q;

  and and_1 (and_1_out, R1w, CLK);
  D_Flip_Flop #(.trigger("falling")) d_ff_1 (.D(dataIn4), .clk(and_1_out), .Q(d_ff_1_q));  // open: Qn, preset, reset
  D_Flip_Flop #(.trigger("falling")) d_ff_2 (.D(dataIn3), .clk(and_1_out), .Q(d_ff_2_q));  // open: Qn, preset, reset
  D_Flip_Flop #(.trigger("falling")) d_ff_3 (.D(dataIn2), .clk(and_1_out), .Q(d_ff_3_q));  // open: Qn, preset, reset
  D_Flip_Flop #(.trigger("falling")) d_ff_4 (.D(dataIn1), .clk(and_1_out), .Q(d_ff_4_q));  // open: Qn, preset, reset
  and and_2 (dataOut4, d_ff_1_q, en);
  and and_3 (dataOut3, d_ff_2_q, en);
  and and_4 (dataOut2, d_ff_3_q, en);
  and and_5 (dataOut1, d_ff_4_q, en);
endmodule

module R2 (
  input  dataIn4,
  input  dataIn3,
  input  dataIn2,
  input  dataIn1,
  input  en,
  input  R2w,
  input  CLK,
  output dataOut4,
  output dataOut3,
  output dataOut2,
  output dataOut1
);

  wire and_1_out, d_ff_1_q, d_ff_2_q, d_ff_3_q, d_ff_4_q;

  and and_1 (and_1_out, R2w, CLK);
  D_Flip_Flop #(.trigger("falling")) d_ff_1 (.D(dataIn4), .clk(and_1_out), .Q(d_ff_1_q));  // open: Qn, preset, reset
  D_Flip_Flop #(.trigger("falling")) d_ff_2 (.D(dataIn3), .clk(and_1_out), .Q(d_ff_2_q));  // open: Qn, preset, reset
  D_Flip_Flop #(.trigger("falling")) d_ff_3 (.D(dataIn2), .clk(and_1_out), .Q(d_ff_3_q));  // open: Qn, preset, reset
  D_Flip_Flop #(.trigger("falling")) d_ff_4 (.D(dataIn1), .clk(and_1_out), .Q(d_ff_4_q));  // open: Qn, preset, reset
  and and_2 (dataOut4, d_ff_1_q, en);
  and and_3 (dataOut3, d_ff_2_q, en);
  and and_4 (dataOut2, d_ff_3_q, en);
  and and_5 (dataOut1, d_ff_4_q, en);
endmodule

module Increment (
  input  a3In,
  input  a2In,
  input  a1In,
  output a3Out,
  output a2Out,
  output a1Out
);

  wire and_1_out, and_2_out;

  xor xor_1 (a3Out, 1'b1, a3In);
  and and_1 (and_1_out, 1'b1, a3In);
  xor xor_2 (a2Out, and_1_out, a2In);
  and and_2 (and_2_out, and_1_out, a2In);
  xor xor_3 (a1Out, and_2_out, a1In);
endmodule

module divide (
  input  CLK,
  input  Ir1,
  input  Ir2,
  output LD,
  output SV,
  output ADD,
  output SUB
);

  wire and_1_out, and_2_out, and_3_out;

  and and_1 (and_1_out, ~Ir1, ~Ir2);  // AND_Gate
  and and_2 (and_2_out, ~Ir1, Ir2);  // AND_Gate
  and and_3 (and_3_out, Ir1, ~Ir2);  // AND_Gate
  and and_4 (SUB, Ir1, Ir2);
  and and_5 (LD, CLK, and_1_out);
  and and_6 (SV, CLK, and_2_out);
  and and_7 (ADD, CLK, and_3_out);
endmodule

module STEP (
  input  CLK,
  input  Reset,
  output Step1,
  output Step2,
  output Step3,
  output Step4,
  output Step5,
  output Step6
);

  wire and_1_out, or_1_out, or_2_out, or_3_out, or_4_out, or_5_out, or_6_out;

  or or_1 (or_1_out, Step6, Step1);
  and and_1 (and_1_out, CLK, ~1'b0);  // AND_Gate
  or or_2 (or_2_out, Step1, Step2);
  T_Flip_Flop #(.trigger("falling")) t_ff_1 (
    .T(or_1_out), .clk(and_1_out), .Q(Step1), .preset(Reset));  // open: Qn, reset
  or or_3 (or_3_out, Step2, Step3);
  T_Flip_Flop #(.trigger("falling")) t_ff_2 (
    .T(or_2_out), .clk(and_1_out), .Q(Step2), .reset(Reset));  // open: Qn, preset
  or or_4 (or_4_out, Step3, Step4);
  T_Flip_Flop #(.trigger("falling")) t_ff_3 (
    .T(or_3_out), .clk(and_1_out), .Q(Step3), .reset(Reset));  // open: Qn, preset
  or or_5 (or_5_out, Step4, Step5);
  T_Flip_Flop #(.trigger("falling")) t_ff_4 (
    .T(or_4_out), .clk(and_1_out), .Q(Step4), .reset(Reset));  // open: Qn, preset
  or or_6 (or_6_out, Step5, Step6);
  T_Flip_Flop #(.trigger("falling")) t_ff_5 (
    .T(or_5_out), .clk(and_1_out), .Q(Step5), .reset(Reset));  // open: Qn, preset
  T_Flip_Flop #(.trigger("falling")) t_ff_6 (
    .T(or_6_out), .clk(and_1_out), .Q(Step6), .reset(Reset));  // open: Qn, preset
endmodule

module IC (
  input  Load,
  input  Save,
  input  Add,
  input  Sub,
  input  Ir3,
  input  Ir4,
  input  CLK,
  input  START,
  output a3,
  output a2,
  output a1,
  output MARw,
  output ALUmode,
  output MBRw,
  output Len,
  output IRw,
  output Lr,
  output Ren,
  output PCadd,
  output PCr,
  output Rr,
  output R1w,
  output ADDRr,
  output R1en,
  output ADDRw,
  output R2w,
  output R2en,
  output RAMen,
  output RAMw
);

  wire and_2_out, and_3_out, and_4_out, and_5_out, and_6_out, and_7_out, and_8_out, and_9_out, and_10_out,
       and_11_out, and_12_out, and_13_out, and_14_out, and_15_out, and_16_out, and_17_out, and_18_out, HALT,
       not_1_out, not_2_out, not_3_out, or_1_out, s4, s5, s6, step_1_step1, step_1_step2, step_1_step3;

  and and_1 (HALT, Sub, Ir3, Ir4);
  or or_1 (or_1_out, Add, Sub);
  not not_1 (not_1_out, Ir3);
  not not_2 (not_2_out, Ir3);
  and and_2 (and_2_out, Load, s4);
  and and_3 (and_3_out, Load, s5);
  and and_4 (and_4_out, Load, s6);
  and and_5 (and_5_out, Save, s4);
  and and_6 (and_6_out, Save, s5);
  and and_7 (and_7_out, Save, s6);
  not not_3 (not_3_out, Ir3);
  and and_8 (and_8_out, CLK, ~HALT);  // AND_Gate
  and and_9 (and_9_out, and_4_out, Ir3);
  and and_10 (and_10_out, and_4_out, not_1_out);
  and and_11 (and_11_out, and_7_out, Ir3);
  and and_12 (and_12_out, and_7_out, not_2_out);
  and and_13 (and_13_out, or_1_out, s4);
  and and_14 (and_14_out, or_1_out, s6);
  and and_15 (and_15_out, or_1_out, s5);
  and and_16 (and_16_out, and_15_out, Ir3);
  and and_17 (and_17_out, and_15_out, not_3_out);
  STEP step_1 (
    .CLK(and_8_out), .Reset(START), .Step1(step_1_step1), .Step2(step_1_step2), .Step3(step_1_step3),
    .Step4(s4), .Step5(s5), .Step6(s6));
  or or_2 (MARw, step_1_step1, and_3_out, and_6_out);
  buf or_3 (MBRw, step_1_step2);  // OR_Gate
  buf or_4 (IRw, step_1_step3);  // OR_Gate
  // OR_Gate or_5 is placed but not wired
  buf or_6 (PCadd, step_1_step1);  // OR_Gate
  buf or_7 (PCr, step_1_step1);  // OR_Gate
  or or_8 (R1w, and_10_out, and_14_out);
  or or_9 (R1en, and_12_out, and_13_out, and_17_out);
  buf or_10 (R2w, and_9_out);  // OR_Gate
  or or_11 (R2en, and_11_out, and_16_out);
  or or_12 (RAMen, and_4_out, step_1_step2);
  or or_13 (RAMw, and_11_out, and_12_out);
  and and_18 (and_18_out, Sub, HALT);
  buf or_14 (ALUmode, and_18_out);  // OR_Gate
  buf or_15 (Len, and_13_out);  // OR_Gate
  buf or_16 (Lr, and_14_out);  // OR_Gate
  or or_17 (Ren, and_16_out, and_17_out);
  buf or_18 (Rr, and_14_out);  // OR_Gate
  or or_19 (ADDRr, and_3_out, and_6_out);
  or or_20 (ADDRw, and_2_out, and_5_out);

  assign a1 = Ir4;
  assign a2 = 1'b0;
  assign a3 = 1'b0;
endmodule

module L (
  input  dataIn4,
  input  dataIn3,
  input  dataIn2,
  input  dataIn1,
  input  Lr,
  input  Len,
  input  CLK,
  output dataOut4,
  output dataOut3,
  output dataOut2,
  output dataOut1
);

  wire and_1_out, d_ff_1_q, d_ff_2_q, d_ff_3_q, d_ff_4_q;

  and and_1 (and_1_out, Len, CLK);
  D_Flip_Flop #(.trigger("falling")) d_ff_1 (.D(dataIn4), .clk(and_1_out), .Q(d_ff_1_q));  // open: Qn, preset, reset
  D_Flip_Flop #(.trigger("falling")) d_ff_2 (.D(dataIn3), .clk(and_1_out), .Q(d_ff_2_q));  // open: Qn, preset, reset
  D_Flip_Flop #(.trigger("falling")) d_ff_3 (.D(dataIn2), .clk(and_1_out), .Q(d_ff_3_q));  // open: Qn, preset, reset
  D_Flip_Flop #(.trigger("falling")) d_ff_4 (.D(dataIn1), .clk(and_1_out), .Q(d_ff_4_q));  // open: Qn, preset, reset
  and and_2 (dataOut4, d_ff_1_q, Lr);
  and and_3 (dataOut3, d_ff_2_q, Lr);
  and and_4 (dataOut2, d_ff_3_q, Lr);
  and and_5 (dataOut1, d_ff_4_q, Lr);
endmodule

module R (
  input  dataIn4,
  input  dataIn3,
  input  dataIn2,
  input  dataIn1,
  input  Rr,
  input  Ren,
  input  CLK,
  output dataOut4,
  output dataOut3,
  output dataOut2,
  output dataOut1
);

  wire and_1_out, d_ff_1_q, d_ff_2_q, d_ff_3_q, d_ff_4_q;

  and and_1 (and_1_out, Ren, CLK);
  D_Flip_Flop #(.trigger("falling")) d_ff_1 (.D(dataIn4), .clk(and_1_out), .Q(d_ff_1_q));  // open: Qn, preset, reset
  D_Flip_Flop #(.trigger("falling")) d_ff_2 (.D(dataIn3), .clk(and_1_out), .Q(d_ff_2_q));  // open: Qn, preset, reset
  D_Flip_Flop #(.trigger("falling")) d_ff_3 (.D(dataIn2), .clk(and_1_out), .Q(d_ff_3_q));  // open: Qn, preset, reset
  D_Flip_Flop #(.trigger("falling")) d_ff_4 (.D(dataIn1), .clk(and_1_out), .Q(d_ff_4_q));  // open: Qn, preset, reset
  and and_2 (dataOut4, d_ff_1_q, Rr);
  and and_3 (dataOut3, d_ff_2_q, Rr);
  and and_4 (dataOut2, d_ff_3_q, Rr);
  and and_5 (dataOut1, d_ff_4_q, Rr);
endmodule
